# Fritzing sketch circuit (saved by Fritzing 0.9.3b)
breadboards: 1

parts:
  Raspberry_Pi_1 = Raspberry Pi 3 [part_number=RPI-3-V1.2]
  Part1 = Arduino Uno (Rev3)
  Part2 = Logic Level Converter
  LCD1 = LCD screen
  S1 = Momentary Switch [package=ksa_sealed_tac_switch]
  S2 = Momentary Switch [package=ksa_sealed_tac_switch]
  S3 = Momentary Switch [package=ksa_sealed_tac_switch]
  S4 = Momentary Switch [package=ksa_sealed_tac_switch]
  S5 = Momentary Switch [package=ksa_sealed_tac_switch]
  R2 = Resistor [tolerance=±5% resistance=220 package="2512 [SMD]"]
  R5 = Resistor [tolerance=±5% resistance=220 package="2512 [SMD]"]
  R6 = Resistor [tolerance=±5% resistance=220 package="2512 [SMD]"]
  R7 = Trimmer Potentiometer [maximum_resistance=10kΩ package=THT]
  R8 = Resistor [tolerance=±5% resistance=220 package="2512 [SMD]"]
  R9 = Resistor [tolerance=±20% resistance=220 package="2512 [SMD]"]

nets:
  N1: Raspberry_Pi_1.3v3, Part2.LV
  GND: Raspberry_Pi_1.GND, Part1.GND, Part2.GND, LCD1.VSS, LCD1.R/W, LCD1.LED-, S3.1
  N2: Raspberry_Pi_1.GIPO15, Part2.TX2_LV
  N3: Raspberry_Pi_1.GIPO14, Part2.RX2_LV
  5V: Raspberry_Pi_1.5V, Part1.VIN, Part2.HV
  N4: Part1.A0, R2.Pin_1, R5.Pin_1, R8.Pin_1, R9.Pin_1
  N5: Part1.D0/RX, Part2.RX2_HV
  N6: Part1.D1/TX, Part2.TX2_HV
  N7: Part1.D2, LCD1.DB4
  N8: Part1.D3_PWM, LCD1.DB5
  N9: Part1.D4, LCD1.DB6
  N10: Part1.D5_PWM, LCD1.DB7
  N11: Part1.D6_PWM, LCD1.RS
  N12: Part1.D7, LCD1.E
  5V_2: Part1.5V, LCD1.VDD, S1.1, S2.1, S4.1, S5.3, R6.Pin_0, R7.wiper
  N13: LCD1.V0, R7.leg1

notes:
  Android Things flashed (with ThingsHVAC app installed)
  up lx dx dw sel
